# Fritzing sketch Untitled Sketch (saved by Fritzing 0.9.3b)
breadboards: 1

parts:
  R1 = PHOTOCELL [package=photocell-kit]
  R2 = Resistor [tolerance=±5% resistance=220 package="0402 [SMD]"]
  Componente1 = Arduino Mega ADK (Rev3)
  LED1 = smd LED [color="Red (633nm)" package="0603 [SMD]"]
  R3 = Resistor [tolerance=±5% resistance=220 package="0402 [SMD]"]

nets:
  N1: R1.P$1, R2.Pin_1, Componente1.A0
  N2: R1.P$2, Componente1.GND, LED1.cathode
  N3: R2.Pin_0, Componente1.5V
  N4: Componente1.D7_PWM, R3.Pin_1
  N5: LED1.anode, R3.Pin_0
